// Logisim project control_logic.circ as structural Verilog: 3 circuits, main circuit control_logic
module control_logic (
  input  [31:0] inst,
  input  BrEq,
  input  BrLt,
  output PCSel,
  output RegWEn,
  output [2:0] ImmSel,
  output BrUn,
  output ASel,
  output BSel,
  output [3:0] ALUSel,
  output MemRW,
  output [1:0] WBSel,
  output CSRSel,
  output CSRWen
);


  assign ALUSel = 4'b0000;
  assign ASel = 1'b0;
  assign BrUn = 1'b0;
  assign BSel = 1'b0;
  assign CSRSel = 1'b0;
  assign CSRWen = 1'b0;
  assign ImmSel = 3'b000;
  assign MemRW = 1'b0;
  assign PCSel = 1'b0;
  assign RegWEn = 1'b0;
  assign WBSel = 2'b00;

  // Notes on the sheet:
  //   INPUTS to your circuit
  //   DON'T CHANGE THE LOCATIONS OF THE INPUTS AND OUTPUTS!
  //   OUTPUT from your circuit
endmodule

module ASel0 (
  input  [4:0] opcode,
  output ASEL_Output
);

  wire AND0_out, AND1_out, AND2_out, not_1_out, not_2_out, not_3_out, not_4_out, not_5_out, not_6_out,
       not_7_out;

  not not_1 (not_1_out, opcode[0]);
  not not_2 (not_2_out, opcode[1]);
  not not_3 (not_3_out, opcode[2]);
  not not_4 (not_4_out, opcode[1]);
  not not_5 (not_5_out, opcode[3]);
  not not_6 (not_6_out, opcode[4]);
  not not_7 (not_7_out, opcode[2]);
  and AND0 (AND0_out, not_1_out, not_2_out, not_3_out, opcode[3], opcode[4]);
  and AND1 (AND1_out, opcode[0], not_4_out, opcode[2], not_5_out, not_6_out);
  // Probe on AND1_out
  and AND2 (AND2_out, opcode[0], opcode[1], not_7_out, opcode[3], opcode[4]);
  or or_1 (ASEL_Output, AND0_out, AND1_out, AND2_out);

  // Other names for the same wires on the sheet: A0 = opcode[0]; A1 = opcode[1]; A2 = opcode[2]; A3 = opcode[3];
  //   A4 = opcode[4]
endmodule

module PCSel0 (
  input  [4:0] opcode,
  input  BrEq,
  input  [2:0] funct3,
  input  BrLt
);
endmodule
